// Logisim project control-logic.circ as structural Verilog: 1 circuit, main circuit control_logic
module control_logic (
  input  [31:0] Instruction,
  input  BrEq,
  input  BrLt,
  output PCSel,
  output RegWEn,
  output [2:0] ImmSel,
  output BrUn,
  output ASel,
  output BSel,
  output [3:0] ALUSel,
  output MemWEn,
  output [1:0] WBSel
);

  wire add, addi, and_1_out, and_2_out, and_3_out, and_4_out, and_5_out, and_6_out, and_i, andi, auipc, beq,
       bge, bgeu, blt, bltu, bne, comparator_1_eq, comparator_2_eq, comparator_3_eq, comparator_4_eq,
       comparator_5_eq, comparator_6_eq, comparator_7_eq, comparator_8_eq, comparator_9_eq, comparator_10_eq,
       comparator_11_eq, comparator_12_eq, comparator_13_eq, comparator_14_eq, comparator_15_eq,
       comparator_16_eq, comparator_17_eq, comparator_18_eq, comparator_19_eq, comparator_20_eq,
       comparator_21_eq, decoder_1_out1, decoder_1_out5, decoder_4_out0, decoder_4_out1, decoder_4_out2,
       decoder_4_out3, decoder_4_out4, decoder_4_out5, decoder_4_out6, decoder_4_out7, jal, jalr, lb, lh,
       lui, lw, mul, mulh, mulhu, not_1_out, not_2_out, not_3_out, or_i, ori, sb, sh, sll_i, slli, slt, slti,
       sra_i, srai, srl_i, srli, sub, sw, xor_i, xori;
  wire [5:0] RomInput;
  wire [15:14] rom_1_data;

  ROM #(.addrWidth(6), .dataWidth(16)) rom_1 (
    .addr(RomInput), .data({rom_1_data, WBSel, MemWEn, ALUSel, BSel, ASel, BrUn, ImmSel, RegWEn}));
  Priority_Encoder #(.select_enc(6)) priority_encoder_1 (
    .in0(add), .in1(mul), .in2(sub), .in3(sll_i), .in4(mulh), .in5(mulhu), .in6(slt), .in7(xor_i),
    .in8(srl_i), .in9(sra_i), .in10(or_i), .in11(and_i), .in12(lb), .in13(lh), .in14(lw), .in15(addi),
    .in16(slli), .in17(slti), .in18(xori), .in19(srli), .in20(srai), .in21(ori), .in22(andi), .in23(sb),
    .in24(sh), .in25(sw), .in26(beq), .in27(bne), .in28(blt), .in29(bge), .in30(bltu), .in31(bgeu),
    .in32(auipc), .in33(lui), .in34(jal), .in35(jalr), .out(RomInput));  // open: in36, in37, in38, in39, in40, in41, in42, in43, in44, in45, in46, in47, in48, in49, in50, in51, in52, in53, in54, in55, in56, in57, in58, in59, in60, in61, in62, in63, gs, en_out, en_in
  Comparator #(.width(7)) comparator_1 (.a(Instruction[6:0]), .b(7'b0010011), .eq(comparator_1_eq));  // open: gt, lt
  Comparator #(.width(7)) comparator_2 (.a(Instruction[6:0]), .b(7'b0000011), .eq(comparator_2_eq));  // open: gt, lt
  Comparator #(.width(7)) comparator_3 (.a(Instruction[6:0]), .b(7'b0100011), .eq(comparator_3_eq));  // open: gt, lt
  Decoder #(.select(3)) decoder_1 (
    .out0(addi), .out1(decoder_1_out1), .out2(slti), .out4(xori), .out5(decoder_1_out5), .out6(ori),
    .out7(andi), .sel(Instruction[14:12]), .en(comparator_1_eq));  // open: out3
  Decoder #(.select(3)) decoder_2 (
    .out0(lb), .out1(lh), .out2(lw), .sel(Instruction[14:12]), .en(comparator_2_eq));  // open: out3, out4, out5, out6, out7
  Decoder #(.select(3)) decoder_3 (
    .out0(sb), .out1(sh), .out2(sw), .sel(Instruction[14:12]), .en(comparator_3_eq));  // open: out3, out4, out5, out6, out7
  Decoder #(.select(3)) decoder_4 (
    .out0(decoder_4_out0), .out1(decoder_4_out1), .out2(decoder_4_out2), .out3(decoder_4_out3),
    .out4(decoder_4_out4), .out5(decoder_4_out5), .out6(decoder_4_out6), .out7(decoder_4_out7),
    .sel(Instruction[14:12]), .en(comparator_4_eq));
  Comparator #(.width(7)) comparator_4 (.a(Instruction[6:0]), .b(7'b0110011), .eq(comparator_4_eq));  // open: gt, lt
  Decoder #(.select(3)) decoder_5 (
    .out0(beq), .out1(bne), .out4(blt), .out5(bge), .out6(bltu), .out7(bgeu), .sel(Instruction[14:12]),
    .en(comparator_5_eq));  // open: out2, out3
  Comparator #(.width(7)) comparator_5 (.a(Instruction[6:0]), .b(7'b1100011), .eq(comparator_5_eq));  // open: gt, lt
  Comparator #(.width(7)) comparator_6 (.a(Instruction[6:0]), .b(7'b1100111), .eq(comparator_6_eq));  // open: gt, lt
  Comparator #(.width(7)) comparator_7 (.a(Instruction[31:25]), .b({7{1'b0}}), .eq(comparator_7_eq));  // open: gt, lt
  Comparator #(.width(7)) comparator_8 (.a(Instruction[31:25]), .b({7{1'b0}}), .eq(comparator_8_eq));  // open: gt, lt
  Comparator #(.width(7)) comparator_9 (.a(Instruction[31:25]), .b(7'b0100000), .eq(comparator_9_eq));  // open: gt, lt
  Decoder #(.select(3)) decoder_6 (
    .out0(jalr), .sel(Instruction[14:12]), .en(comparator_6_eq));  // open: out1, out2, out3, out4, out5, out6, out7
  and and_1 (and_1_out, beq, BrEq);
  and and_2 (and_2_out, bne, not_1_out);
  not not_1 (not_1_out, BrEq);
  and and_3 (and_3_out, blt, BrLt);
  and and_4 (and_4_out, bge, not_2_out);
  not not_2 (not_2_out, BrLt);
  and and_5 (and_5_out, bltu, BrLt);
  and and_6 (and_6_out, bgeu, not_3_out);
  not not_3 (not_3_out, BrLt);
  and and_7 (slli, comparator_7_eq, decoder_1_out1);
  and and_8 (srli, comparator_8_eq, decoder_1_out5);
  and and_9 (srai, comparator_9_eq, decoder_1_out5);
  Comparator #(.width(7)) comparator_10 (.a(Instruction[31:25]), .b({7{1'b0}}), .eq(comparator_10_eq));  // open: gt, lt
  Comparator #(.width(7)) comparator_11 (
    .a(Instruction[31:25]), .b(7'b0000001), .eq(comparator_11_eq));  // open: gt, lt
  Comparator #(.width(7)) comparator_12 (
    .a(Instruction[31:25]), .b(7'b0100000), .eq(comparator_12_eq));  // open: gt, lt
  Comparator #(.width(7)) comparator_13 (.a(Instruction[31:25]), .b({7{1'b0}}), .eq(comparator_13_eq));  // open: gt, lt
  Comparator #(.width(7)) comparator_14 (
    .a(Instruction[31:25]), .b(7'b0000001), .eq(comparator_14_eq));  // open: gt, lt
  Comparator #(.width(7)) comparator_15 (
    .a(Instruction[31:25]), .b(7'b0000001), .eq(comparator_15_eq));  // open: gt, lt
  Comparator #(.width(7)) comparator_16 (.a(Instruction[31:25]), .b({7{1'b0}}), .eq(comparator_16_eq));  // open: gt, lt
  Comparator #(.width(7)) comparator_17 (.a(Instruction[31:25]), .b({7{1'b0}}), .eq(comparator_17_eq));  // open: gt, lt
  Comparator #(.width(7)) comparator_18 (.a(Instruction[31:25]), .b({7{1'b0}}), .eq(comparator_18_eq));  // open: gt, lt
  Comparator #(.width(7)) comparator_19 (
    .a(Instruction[31:25]), .b(7'b0100000), .eq(comparator_19_eq));  // open: gt, lt
  Comparator #(.width(7)) comparator_20 (.a(Instruction[31:25]), .b({7{1'b0}}), .eq(comparator_20_eq));  // open: gt, lt
  Comparator #(.width(7)) comparator_21 (.a(Instruction[31:25]), .b({7{1'b0}}), .eq(comparator_21_eq));  // open: gt, lt
  or or_1 (PCSel, and_1_out, and_2_out, and_3_out, and_4_out, and_5_out, and_6_out, jal, jalr);
  and and_10 (add, comparator_10_eq, decoder_4_out0);
  and and_11 (mul, comparator_11_eq, decoder_4_out0);
  and and_12 (sub, comparator_12_eq, decoder_4_out0);
  and and_13 (sll_i, comparator_13_eq, decoder_4_out1);
  and and_14 (mulh, comparator_14_eq, decoder_4_out1);
  and and_15 (mulhu, comparator_15_eq, decoder_4_out3);
  and and_16 (slt, comparator_16_eq, decoder_4_out2);
  and and_17 (xor_i, comparator_17_eq, decoder_4_out4);
  and and_18 (srl_i, comparator_18_eq, decoder_4_out5);
  and and_19 (sra_i, comparator_19_eq, decoder_4_out5);
  and and_20 (or_i, comparator_20_eq, decoder_4_out6);
  and and_21 (and_i, comparator_21_eq, decoder_4_out7);
  Comparator #(.width(7)) comparator_22 (.a(Instruction[6:0]), .b(7'b0010111), .eq(auipc));  // open: gt, lt
  Comparator #(.width(7)) comparator_23 (.a(Instruction[6:0]), .b(7'b0110111), .eq(lui));  // open: gt, lt
  Comparator #(.width(7)) comparator_24 (.a(Instruction[6:0]), .b(7'b1101111), .eq(jal));  // open: gt, lt

  // Other names for the same wires on the sheet: funct3[2:0] = Instruction[14:12];
  //   funct10[9:0] = {Instruction[31:25], Instruction[14:12]}; funct7[6:0] = Instruction[31:25];
  //   opcode[6:0] = Instruction[6:0]

  // Notes on the sheet:
  //   INPUTS to your circuit
  //   Connect ROM Input here ->
  //   contents of rom_1 (hex, n*v repeats v):
  //   1001 1401 1601 1081 1481 1581 1101 1201 1281 1681 1301 1381 41 41 41 1041 10c1 1141 1241 12c1 16c1
  //   1341 13c1 2842 2842 2842 4*2064 2074 2074 1067 17e7 2069 2041
  //   ROM FOR CONTROL LOGIC
  //   DON'T CHANGE THE LOCATIONS OF THE INPUTS AND OUTPUTS!
  //   This is only if you choose to do the ROM option
  //   CONNECT
  //   WIRE
  //   TO
  //   USE
  //   ROM
  //   OUTPUT from your circuit
  //   Reminder: If using ROM, use combinational logic for PCSel
endmodule
