// Logisim project partial-load.circ as structural Verilog: 1 circuit, main circuit partial_load
module partial_load (
  input  [31:0] Instruction,
  input  [31:0] MemAddress,
  input  [31:0] DataFromMem,
  output [31:0] DataToReg
);

  wire [31:0] multiplexer_1_out, multiplexer_2_out;

  Multiplexer #(.select(2), .width(32)) multiplexer_1 (
    .in0({{25{DataFromMem[7]}}, DataFromMem[6:0]}), .in1({{25{DataFromMem[15]}}, DataFromMem[14:8]}),
    .in2({{25{DataFromMem[23]}}, DataFromMem[22:16]}), .in3({{25{DataFromMem[31]}}, DataFromMem[30:24]}),
    .out(multiplexer_1_out), .sel(MemAddress[1:0]));
  Multiplexer #(.select(2), .width(32)) multiplexer_2 (
    .in0({{17{DataFromMem[15]}}, DataFromMem[14:0]}), .in1({{17{DataFromMem[23]}}, DataFromMem[22:8]}),
    .in2({{17{DataFromMem[31]}}, DataFromMem[30:16]}), .out(multiplexer_2_out), .sel(MemAddress[1:0]));  // open: in3
  Multiplexer #(.select(3), .width(32)) multiplexer_3 (
    .in0(multiplexer_1_out), .in1(multiplexer_2_out), .in2(DataFromMem), .out(DataToReg),
    .sel(Instruction[14:12]));  // open: in3, in4, in5, in6, in7

  // Notes on the sheet:
  //   INPUTS to your circuit
  //   DON'T CHANGE THE LOCATIONS OF THE INPUTS AND OUTPUTS!
  //   OUTPUT from your circuit
endmodule
