// Logisim project regfile.circ as structural Verilog: 1 circuit, main circuit regfile
module regfile (
  input  [4:0] ReadIndex1,
  input  [4:0] ReadIndex2,
  input  [4:0] WriteIndex,
  input  [31:0] WriteData,
  input  RegWEn,
  input  clk,
  output [31:0] ra,
  output [31:0] sp,
  output [31:0] t0,
  output [31:0] t1,
  output [31:0] t2,
  output [31:0] s0,
  output [31:0] s1,
  output [31:0] a0,
  output [31:0] ReadData1,
  output [31:0] ReadData2
);

  wire ua0, ua1, ua2, ua3, ua4, ua5, ua6, ua7, ugp, ura, us0, us1, us2, us3, us4, us5, us6, us7, us8, us9,
       us10, us11, usp, ut0, ut1, ut2, ut3, ut4, ut5, ut6, utp;
  wire [31:0] a1, a2, a3, a4, a5, a6, a7, gp, s2, s3, s4, s5, s6, s7, s8, s9, s10, s11, t3, t4, t5, t6, tp;

  Multiplexer #(.select(5), .width(32)) multiplexer_1 (
    .in0({32{1'b0}}), .in1(ra), .in2(sp), .in3(gp), .in4(tp), .in5(t0), .in6(t1), .in7(t2), .in8(s0),
    .in9(s1), .in10(a0), .in11(a1), .in12(a2), .in13(a3), .in14(a4), .in15(a5), .in16(a6), .in17(a7),
    .in18(s2), .in19(s3), .in20(s4), .in21(s5), .in22(s6), .in23(s7), .in24(s8), .in25(s9), .in26(s10),
    .in27(s11), .in28(t3), .in29(t4), .in30(t5), .in31(t6), .out(ReadData1), .sel(ReadIndex1));
  Demultiplexer #(.select(5)) demultiplexer_1 (
    .out1(ura), .out2(usp), .out3(ugp), .out4(utp), .out5(ut0), .out6(ut1), .out7(ut2), .out8(us0),
    .out9(us1), .out10(ua0), .out11(ua1), .out12(ua2), .out13(ua3), .out14(ua4), .out15(ua5), .out16(ua6),
    .out17(ua7), .out18(us2), .out19(us3), .out20(us4), .out21(us5), .out22(us6), .out23(us7), .out24(us8),
    .out25(us9), .out26(us10), .out27(us11), .out28(ut3), .out29(ut4), .out30(ut5), .out31(ut6), .in(RegWEn),
    .sel(WriteIndex));  // open: out0
  Multiplexer #(.select(5), .width(32)) multiplexer_2 (
    .in0({32{1'b0}}), .in1(ra), .in2(sp), .in3(gp), .in4(tp), .in5(t0), .in6(t1), .in7(t2), .in8(s0),
    .in9(s1), .in10(a0), .in11(a1), .in12(a2), .in13(a3), .in14(a4), .in15(a5), .in16(a6), .in17(a7),
    .in18(s2), .in19(s3), .in20(s4), .in21(s5), .in22(s6), .in23(s7), .in24(s8), .in25(s9), .in26(s10),
    .in27(s11), .in28(t3), .in29(t4), .in30(t5), .in31(t6), .out(ReadData2), .sel(ReadIndex2));
  Register #(.width(32)) register_1 (.D(WriteData), .en(ura), .clk(clk), .Q(ra));  // open: clr
  Register #(.width(32)) register_2 (.D(WriteData), .en(usp), .clk(clk), .Q(sp));  // open: clr
  Register #(.width(32)) register_3 (.D(WriteData), .en(ugp), .clk(clk), .Q(gp));  // open: clr
  Register #(.width(32)) register_4 (.D(WriteData), .en(utp), .clk(clk), .Q(tp));  // open: clr
  Register #(.width(32)) register_5 (.D(WriteData), .en(ut0), .clk(clk), .Q(t0));  // open: clr
  Register #(.width(32)) register_6 (.D(WriteData), .en(ut1), .clk(clk), .Q(t1));  // open: clr
  Register #(.width(32)) register_7 (.D(WriteData), .en(ut2), .clk(clk), .Q(t2));  // open: clr
  Register #(.width(32)) register_8 (.D(WriteData), .en(us0), .clk(clk), .Q(s0));  // open: clr
  Register #(.width(32)) register_9 (.D(WriteData), .en(us1), .clk(clk), .Q(s1));  // open: clr
  Register #(.width(32)) register_10 (.D(WriteData), .en(ua0), .clk(clk), .Q(a0));  // open: clr
  Register #(.width(32)) register_11 (.D(WriteData), .en(ua1), .clk(clk), .Q(a1));  // open: clr
  Register #(.width(32)) register_12 (.D(WriteData), .en(ua2), .clk(clk), .Q(a2));  // open: clr
  Register #(.width(32)) register_13 (.D(WriteData), .en(ua3), .clk(clk), .Q(a3));  // open: clr
  Register #(.width(32)) register_14 (.D(WriteData), .en(ua4), .clk(clk), .Q(a4));  // open: clr
  Register #(.width(32)) register_15 (.D(WriteData), .en(ua5), .clk(clk), .Q(a5));  // open: clr
  Register #(.width(32)) register_16 (.D(WriteData), .en(ua6), .clk(clk), .Q(a6));  // open: clr
  Register #(.width(32)) register_17 (.D(WriteData), .en(ua7), .clk(clk), .Q(a7));  // open: clr
  Register #(.width(32)) register_18 (.D(WriteData), .en(us2), .clk(clk), .Q(s2));  // open: clr
  Register #(.width(32)) register_19 (.D(WriteData), .en(us3), .clk(clk), .Q(s3));  // open: clr
  Register #(.width(32)) register_20 (.D(WriteData), .en(us4), .clk(clk), .Q(s4));  // open: clr
  Register #(.width(32)) register_21 (.D(WriteData), .en(us5), .clk(clk), .Q(s5));  // open: clr
  Register #(.width(32)) register_22 (.D(WriteData), .en(us6), .clk(clk), .Q(s6));  // open: clr
  Register #(.width(32)) register_23 (.D(WriteData), .en(us7), .clk(clk), .Q(s7));  // open: clr
  Register #(.width(32)) register_24 (.D(WriteData), .en(us8), .clk(clk), .Q(s8));  // open: clr
  Register #(.width(32)) register_25 (.D(WriteData), .en(us9), .clk(clk), .Q(s9));  // open: clr
  Register #(.width(32)) register_26 (.D(WriteData), .en(us10), .clk(clk), .Q(s10));  // open: clr
  Register #(.width(32)) register_27 (.D(WriteData), .en(us11), .clk(clk), .Q(s11));  // open: clr
  Register #(.width(32)) register_28 (.D(WriteData), .en(ut3), .clk(clk), .Q(t3));  // open: clr
  Register #(.width(32)) register_29 (.D(WriteData), .en(ut4), .clk(clk), .Q(t4));  // open: clr
  Register #(.width(32)) register_30 (.D(WriteData), .en(ut5), .clk(clk), .Q(t5));  // open: clr
  Register #(.width(32)) register_31 (.D(WriteData), .en(ut6), .clk(clk), .Q(t6));  // open: clr

  // Notes on the sheet:
  //   INPUTS to your circuit
  //   DON'T CHANGE THE LOCATIONS OF THE INPUTS AND OUTPUTS!
  //   These are DEBUG/TEST outputs from your circuit.
  //   OUTPUTS from your circuit
endmodule
